// Digital circuit main.dig as structural Verilog
module main (
  input  Clock
);

  wire addrspacedivider_1_isel, addrspacedivider_1_read, addrspacedivider_1_write, addrspacedivider_2_isel,
       addrspacedivider_2_read, addrspacedivider_2_write, addrspacedivider_3_read, addrspacedivider_3_write,
       and_1_out, Clock_t, ClockMode_out, cpu_1_stalls, d_ff_1_q, demultiplexer_1_out_0,
       demultiplexer_1_out_1, demultiplexer_1_out_2, demultiplexer_1_out_3, MemEnable, MemWrite,
       PowOnReset_out, Pulse_out, Reset, Reset_out;
  wire [1:0] cpu_1_memsize;
  wire [13:0] addrspacedivider_1_addrlow, addrspacedivider_1_iaddrlow, addrspacedivider_2_addrlow,
       addrspacedivider_2_iaddrlow, addrspacedivider_3_addrlow;
  wire [15:0] addrspacedivider_1_nextaddrspace;
  wire [19:0] register_1_q;
  wire [29:0] Addr, IAddr;
  wire [31:0] cpu_1_address, cpu_1_dataout, cpu_1_iaddr, DataIn, IDataIn, MemDataIn, MemDataOut, MemIDataOut,
       ramdualaccess_1_d2, ramdualaccess_2_d2;
  wire [63:0] barrelshifter_1_out, counter_1_out, counter_2_out, div_1_q;

  DipSwitch ClockMode (.out(ClockMode_out));
  Button Pulse (.out(Pulse_out));
  Button u_Reset (.out(Reset_out));
  Reset #(.invertOutput("false")) PowOnReset (.out(PowOnReset_out));
  Multiplexer multiplexer_1 (.sel(ClockMode_out), .in_0(Pulse_out), .in_1(Clock), .out(Clock_t));
  or or_1 (Reset, Reset_out, PowOnReset_out);
  CPU cpu_1 (
    .DataIn(DataIn), .InstructionIn(IDataIn), .Enable(1'b1), .Clock(Clock_t), .Reset(Reset),
    .DataOut(cpu_1_dataout), .Address(cpu_1_address), .MemEnable(MemEnable), .MemWrite(MemWrite),
    .MemSize(cpu_1_memsize), .IAddr(cpu_1_iaddr), .Stalls(cpu_1_stalls));
  Counter #(.Bits(64)) counter_1 (.en(cpu_1_stalls), .C(Clock_t), .clr(1'b0), .out(counter_1_out));  // open: ovf
  Counter #(.Bits(64)) counter_2 (.en(1'b1), .C(Clock_t), .clr(1'b0), .out(counter_2_out));  // open: ovf
  BarrelShifter #(.Bits(64)) barrelshifter_1 (.in(counter_1_out), .shift(7'b0010000), .out(barrelshifter_1_out));
  Div #(.Bits(64)) div_1 (.a(barrelshifter_1_out), .b(counter_2_out), .q(div_1_q));  // open: r
  // Probe on counter_1_out
  // Probe on counter_2_out
  // Probe on div_1_q
  MemoryDriver memorydriver_1 (
    .CPUDataIn(cpu_1_dataout), .AddrIn(cpu_1_address), .MemDataIn(MemDataOut), .MemIDataIn(MemIDataOut),
    .Size(cpu_1_memsize), .IAddrIn(cpu_1_iaddr), .AddrOut(Addr), .IAddrOut(IAddr), .MemIDataOut(IDataIn),
    .WriteDataOut(MemDataIn), .ReadDataOut(DataIn));
  AddrSpaceDivider addrspacedivider_1 (
    .HighAddrSpace({16{1'b0}}), .Addr(Addr), .IAddr(IAddr), .MemEnable(MemEnable), .IEnable(1'b1),
    .WriteIn(MemWrite), .Write(addrspacedivider_1_write), .Read(addrspacedivider_1_read),
    .AddrLow(addrspacedivider_1_addrlow), .IAddrLow(addrspacedivider_1_iaddrlow),
    .ISel(addrspacedivider_1_isel), .NextAddrSpace(addrspacedivider_1_nextaddrspace));
  AddrSpaceDivider addrspacedivider_2 (
    .HighAddrSpace(addrspacedivider_1_nextaddrspace), .Addr(Addr), .IAddr(IAddr), .MemEnable(MemEnable),
    .IEnable(1'b1), .WriteIn(MemWrite), .Write(addrspacedivider_2_write), .Read(addrspacedivider_2_read),
    .AddrLow(addrspacedivider_2_addrlow), .IAddrLow(addrspacedivider_2_iaddrlow),
    .ISel(addrspacedivider_2_isel));  // open: NextAddrSpace
  AddrSpaceDivider addrspacedivider_3 (
    .HighAddrSpace({16{1'b1}}), .Addr(Addr), .IAddr(IAddr), .MemEnable(MemEnable), .IEnable(1'b1),
    .WriteIn(MemWrite), .Write(addrspacedivider_3_write), .Read(addrspacedivider_3_read),
    .AddrLow(addrspacedivider_3_addrlow));  // open: IAddrLow, ISel, NextAddrSpace
  assign MemDataOut = addrspacedivider_3_read ? {32{1'b0}} : 32'bz;  // Driver driver_1
  and and_1 (and_1_out, addrspacedivider_3_write, addrspacedivider_3_read);
  RAMDualAccess #(.AddrBits(14), .isProgramMemory("true"), .Bits(32)) ramdualaccess_1 (
    .str(addrspacedivider_1_write), .C(Clock_t), .ld(addrspacedivider_1_read),
    .A1(addrspacedivider_1_addrlow), .Din1(MemDataIn), .A2(addrspacedivider_1_iaddrlow), .D1(MemDataOut),
    .D2(ramdualaccess_1_d2));
  RAMDualAccess #(.AddrBits(14), .Bits(32)) ramdualaccess_2 (
    .str(addrspacedivider_2_write), .C(Clock_t), .ld(addrspacedivider_2_read),
    .A1(addrspacedivider_2_addrlow), .Din1(MemDataIn), .A2(addrspacedivider_2_iaddrlow), .D1(MemDataOut),
    .D2(ramdualaccess_2_d2));
  Demultiplexer #(.Selector_Bits(4)) demultiplexer_1 (
    .sel(addrspacedivider_3_addrlow[3:0]), .in(and_1_out), .out_0(demultiplexer_1_out_0),
    .out_1(demultiplexer_1_out_1), .out_2(demultiplexer_1_out_2), .out_3(demultiplexer_1_out_3));  // open: out_4, out_5, out_6, out_7, out_8, out_9, out_10, out_11, out_12, out_13, out_14, out_15
  assign MemIDataOut = addrspacedivider_1_isel ? ramdualaccess_1_d2 : 32'bz;  // Driver driver_2
  assign MemIDataOut = addrspacedivider_2_isel ? ramdualaccess_2_d2 : 32'bz;  // Driver driver_3
  Terminal terminal_1 (.D(MemDataIn[6:0]), .C(Clock_t), .en(demultiplexer_1_out_0));
  Register #(.Bits(20)) register_1 (.D(MemDataIn[19:0]), .C(Clock_t), .en(demultiplexer_1_out_1), .Q(register_1_q));
  D_FF d_ff_1 (.D(demultiplexer_1_out_3), .C(Clock_t), .Q(d_ff_1_q));  // open: nQ
  GraphicCard #(.graphicHeight(480), .graphicWidth(640)) graphiccard_1 (
    .A(register_1_q), .str(demultiplexer_1_out_2), .C(Clock_t), .ld(1'b0), .B(d_ff_1_q), .D(MemDataIn[0]));

  // Notes on the sheet:
  //   Clock: Hz: 50000
endmodule
